# Fritzing sketch LED MOSFET board (saved by Fritzing 0.8.5b)
breadboards: 1

parts:
  Q1 = Basic FET P-Channel [package="TO220 [THT]"]
  Opto-Iso = MOC3031-M [package=dil06]
  R2 = Resistor [tolerance=±5% resistance=33k package=THT]
  LED_terminals = Screw terminal - 2 pins [package=THT]
  PWM_input = Screw terminal - 2 pins [package=THT]
  R1 = Resistor [tolerance=±5% resistance=500 package=THT]
  C1 = Ceramic Capacitor [capacitance=100nF package="100 mil [THT, multilayer]"]  # not connected

nets:
  N1: Q1.gate, Opto-Iso.1, Opto-Iso.6, R2.Pin_1, R1.Pin_1
  N2: Q1.drain, LED_terminals.pin2
  GND: Q1.source, Opto-Iso.4
  N3: Opto-Iso.2, PWM_input.pin1
  33V: R2.Pin_0, LED_terminals.pin1
  N4: PWM_input.pin2, R1.Pin_0
